# Fritzing sketch Puffatron (saved by Fritzing 1.0.1rc)
circuit board: 8.46667cm x 5.64444cm
breadboards: 1

parts:
  A1 = Waveshare rp2040-zero tht [package=THT]
  Part1 = OLED Monochrome 128x64 0.96 inch [part_number=326]
  Part2 = Adafruit PCA9685 PWM/Servo Breakout [part_number=815]
  Part3 = Adafruit PCA9685 PWM/Servo Breakout [part_number=815]
  IC1 = ULN2803A [package=THT]
  IC3 = ULN2803A [package=THT]
  IC4 = ULN2803A [package=THT]
  IC5 = ULN2803A [package=THT]
  IC6 = ULN2803A [package=THT]
  L1 = Solenoid
  Power_plug1 = Power plug

nets:
  GND: A1.Pin_2, Part1.GND, Part2.GND, Part3.GND, IC1.0V, IC3.0V, IC4.0V, IC5.0V, IC6.0V, Power_plug1.GND
  VCC: A1.Pin_3, Part1.3.3V, Part2.VCC, Part3.VCC
  N1: A1.Pin_4, Part2.SCL, Part3.SCL
  N2: A1.Pin_5, Part2.SDA, Part3.SDA
  N3: A1.Pin_6, Part1.SCLK_SCK
  N4: A1.Pin_7, Part1.MOSI_SDA
  N5: A1.Pin_16, IC5.In_8
  N6: A1.Pin_17, IC5.In_7
  N7: A1.Pin_18, IC5.In_6
  N8: A1.Pin_19, IC5.In_5
  N9: A1.Pin_20, IC5.In_4
  N10: A1.Pin_21, IC5.In_3
  N11: A1.Pin_22, IC5.In_2
  N12: A1.Pin_23, IC5.In_1
  N13: Part2.PWM7, IC6.In_1
  N14: Part2.PWM6, IC6.In_2
  N15: Part2.PWM5, IC6.In_3
  N16: Part2.PWM4, IC6.In_4
  N17: Part2.PWM3, IC6.In_5
  N18: Part2.PWM2, IC6.In_6
  N19: Part2.PWM1, IC6.In_7
  N20: Part2.PWM0, IC6.In_8
  N21: Part2.PWM15, IC4.In_1
  N22: Part2.PWM14, IC4.In_2
  N23: Part2.PWM13, IC4.In_3
  N24: Part2.PWM12, IC4.In_4
  N25: Part2.PWM11, IC4.In_5
  N26: Part2.PWM10, IC4.In_6
  N27: Part2.PWM9, IC4.In_7
  N28: Part2.PWM8, IC4.In_8
  N29: Part3.PWM7, IC1.In_1
  N30: Part3.PWM6, IC1.In_2
  N31: Part3.PWM5, IC1.In_3
  N32: Part3.PWM4, IC1.In_4
  N33: Part3.PWM3, IC1.In_5
  N34: Part3.PWM2, IC1.In_6
  N35: Part3.PWM1, IC1.In_7
  N36: Part3.PWM0, IC1.In_8
  N37: Part3.PWM15, IC3.In_1
  N38: Part3.PWM14, IC3.In_2
  N39: Part3.PWM13, IC3.In_3
  N40: Part3.PWM12, IC3.In_4
  N41: Part3.PWM11, IC3.In_5
  N42: Part3.PWM10, IC3.In_6
  N43: Part3.PWM9, IC3.In_7
  N44: Part3.PWM8, IC3.In_8
  N45: IC1.COM_-_Common, IC3.COM_-_Common, IC4.COM_-_Common, IC5.COM_-_Common, IC6.COM_-_Common, L1.pin2, Power_plug1.VCC
  N46: IC5.Out_1, L1.pin1

notes:
  Bridge A0 Pads
  DO NOT connect the left and right positive rails!
  The left rail is 3V3 for the modules.
  The right rail is c.10V for the solenoids.

custom parts:
  Waveshare rp2040-zero tht: .RP2040-Zero, A Low-Cost, High-Performance Pico-Like MCU Board Based On Raspberry Pi Microcontroller RP2040. This varant is THT without the extra connections.
